# Fritzing sketch C&C Experiemnt 1 (saved by Fritzing 1.0.3b)
breadboards: 1

parts:
  M1 = Arduino NANO RP2040 CONNECT with headers
  LED3 = smd LED [color="White (4500K)" package="1206 [SMD]"]
  LED8 = smd LED [color="White (4500K)" package="1206 [SMD]"]
  LED9 = smd LED [color="White (4500K)" package="1206 [SMD]"]
  LED10 = smd LED [color="White (4500K)" package="1206 [SMD]"]
  LED11 = smd LED [color="White (4500K)" package="1206 [SMD]"]
  LED12 = smd LED [color="White (4500K)" package="1206 [SMD]"]
  LED13 = smd LED [color="White (4500K)" package="1206 [SMD]"]
  LED14 = smd LED [color="White (4500K)" package="1206 [SMD]"]
  J1 = Basic Force Sensing Resistor (FSR) [package=THT]
  J2 = Basic Force Sensing Resistor (FSR) [package=THT]
  R1 = Resistor [tolerance=±5% resistance=10k package="1206 [SMD]"]
  R2 = Resistor [tolerance=±5% resistance=10k package="1206 [SMD]"]

nets:
  N1: M1.GND-4, M1.GND-29, LED3.cathode, LED8.cathode, LED9.cathode, LED10.cathode, LED11.cathode, LED12.cathode, R1.Pin_1, R2.Pin_1
  N2: M1.D2, LED3.anode, LED8.anode
  N3: M1.D3, LED9.anode, LED10.anode
  N4: M1.D4, LED11.anode, LED12.anode
  N5: M1.D5, LED13.anode, LED14.anode
  N6: M1.+3V3, J1.pin_0, J2.pin_0
  N7: M1.AREF, J1.pin_1
  N8: M1.D14, R1.Pin_0
  N9: M1.D18, J2.pin_1, R2.Pin_0
  N10: LED13.cathode, LED14.cathode
